# Fritzing sketch protecaoServo (saved by Fritzing 0.9.4)
breadboards: 2

parts:
  Componente1 = Arduino Uno (Rev3)
  U1 = LM358 [package=dip08]
  R1 = Resistor [tolerance=±5% resistance=22k package=THT]
  R2 = Resistor [tolerance=±5% resistance=22k package=THT]
  R3 = Resistor [tolerance=±5% resistance=1k package=THT]
  R4 = Resistor [tolerance=±5% resistance=1k package=THT]
  C1 = Electrolytic Capacitor [capacitance=1mF voltage=16V package="100 mil [THT, electrolytic]"]
  R6 = Rotary Potentiometer (Small) [maximum_resistance=0.2MΩ package=THT]
  R7 = Rotary Potentiometer (Small) [maximum_resistance=0.2MΩ package=THT]
  R8 = Rotary Potentiometer (Small) [maximum_resistance=0.2MΩ package=THT]
  R9 = Rotary Potentiometer (Small) [maximum_resistance=0.2MΩ package=THT]
  R10 = Resistor [tolerance=±5% resistance=4.7k package=THT]
  R11 = Resistor [tolerance=±5% resistance=2.7k package=THT]
  C2 = Electrolytic Capacitor [capacitance=1µF voltage=50V package="100 mil [THT, electrolytic]"]
  R12 = Resistor 3W [tolerance=±5% power=5W resistance=0.1 package=THT]
  R13 = Resistor 3W [tolerance=±5% power=5W resistance=0.1 package=THT]
  Power_plug1 = Power plug
  J1 = Basic Servo
  J2 = Basic Servo
  J3 = Basic Servo
  J4 = Basic Servo

nets:
  N1: Componente1.A0, R6.wiper
  N2: Componente1.A1, R9.wiper
  N3: Componente1.A2, R8.wiper
  N4: Componente1.A3, R7.wiper
  N5: Componente1.A4/SDA, U1.G$2_OUT, R2.Pin_0
  N6: Componente1.A5/SCL, U1.G$1_OUT, R1.Pin_0
  N7: Componente1.D9_PWM, J1.pulse
  N8: Componente1.D10_PWM/SS, J3.pulse
  N9: Componente1.D11_PWM/MOSI, J4.pulse
  N10: Componente1.AREF, R6.leg2, R7.leg2, R8.leg2, R9.leg2, R10.Pin_1, R11.Pin_0, C2.+
  N11: Componente1.D6_PWM, J2.pulse
  N12: Componente1.5V, U1.G$1_V+, C1.+, R10.Pin_0
  GND: Componente1.GND, R3.Pin_0, R4.Pin_1, R12.Pin_1, R13.Pin_1, Power_plug1.GND, J1.gnd, J3.gnd
  N13: U1.G$1_-IN, R1.Pin_1, R4.Pin_0
  N14: U1.G$1_+IN, R12.Pin_0, J2.gnd
  VCC: U1.G$1_V-, C1.-, Power_plug1.VCC, J1.vcc, J2.vcc, J3.vcc, J4.vcc
  N15: U1.G$2_+IN, R13.Pin_0, J4.gnd
  N16: U1.G$2_-IN, R2.Pin_1, R3.Pin_1
  N17: R6.leg1, R7.leg1, R8.leg1, R9.leg1, R11.Pin_1, C2.-

custom parts:
  220 Ω Resistor 3W: A generic resistor (3W metal film)
